// Digital circuit boolean-unit.dig as structural Verilog
module boolean_unit (
  input  [31:0] A,
  input  [31:0] B,
  input  [1:0] Bool,
  output [31:0] Out
);

  wire [31:0] and_1_out, or_1_out, xor_1_out;

  assign and_1_out = A & B;  // And and_1, 32 bits wide
  assign or_1_out = A | B;  // Or or_1, 32 bits wide
  assign xor_1_out = A ^ B;  // XOr xor_1, 32 bits wide
  Multiplexer #(.Bits(32), .Selector_Bits(2)) multiplexer_1 (
    .sel(Bool), .in_0(and_1_out), .in_1(or_1_out), .in_2(xor_1_out), .in_3({32{1'b0}}), .out(Out));
endmodule

/* Test case boolean-unit tests:
A B Bool Out
0x00000000 0x00000000 0 0x00000000
0x00000000 0x00000000 1 0x00000000
0x00000000 0x00000000 2 0x00000000
0x00000000 0x00000001 0 0x00000000
0x00000000 0x00000001 1 0x00000001
0x00000000 0x00000001 2 0x00000001
0x00000001 0x00000000 0 0x00000000
0x00000001 0x00000000 1 0x00000001
0x00000001 0x00000000 2 0x00000001
0x00000001 0x00000001 0 0x00000001
0x00000001 0x00000001 1 0x00000001
0x00000001 0x00000001 2 0x00000000
0x00000004 0x00000005 0 0x00000004
0x00000004 0x00000005 1 0x00000005
0x00000004 0x00000005 2 0x00000001
0x00000003 0x00000001 0 0x00000001
0x00000003 0x00000001 1 0x00000003
0x00000003 0x00000001 2 0x00000002
0xFFFFFFFF 0x00000001 0 0x00000001
0xFFFFFFFF 0x00000001 1 0xFFFFFFFF
0xFFFFFFFF 0x00000001 2 0xFFFFFFFE
0x7FFFFFFF 0x00000001 0 0x00000001
0x7FFFFFFF 0x00000001 1 0x7FFFFFFF
0x7FFFFFFF 0x00000001 2 0x7FFFFFFE
0x80000000 0x00000001 0 0x00000000
0x80000000 0x00000001 1 0x80000001
0x80000000 0x00000001 2 0x80000001
0x00000000 0x80000000 0 0x00000000
0x00000000 0x80000000 1 0x80000000
0x00000000 0x80000000 2 0x80000000
0x80000000 0xFFFFFFFF 0 0x80000000
0x80000000 0xFFFFFFFF 1 0xFFFFFFFF
0x80000000 0xFFFFFFFF 2 0x7FFFFFFF
0x7FFFFFFF 0xFFFFFFFF 0 0x7FFFFFFF
0x7FFFFFFF 0xFFFFFFFF 1 0xFFFFFFFF
0x7FFFFFFF 0xFFFFFFFF 2 0x80000000
0x80000000 0x80000000 0 0x80000000
0x80000000 0x80000000 1 0x80000000
0x80000000 0x80000000 2 0x00000000
0xFFFFFFFF 0xFFFFFFFF 0 0xFFFFFFFF
0xFFFFFFFF 0xFFFFFFFF 1 0xFFFFFFFF
0xFFFFFFFF 0xFFFFFFFF 2 0x00000000
0xA5A5A5A5 0x0F0F0F0F 0 0x05050505
0xA5A5A5A5 0x0F0F0F0F 1 0xAFAFAFAF
0xA5A5A5A5 0x0F0F0F0F 2 0xAAAAAAAA
0x65271812 0xDE772179 0 0x44270010
0x65271812 0xDE772179 1 0xFF77397B
0x65271812 0xDE772179 2 0xBB50396B
0xD40719BE 0x2D28E457 0 0x04000016
0xD40719BE 0x2D28E457 1 0xFD2FFDFF
0xD40719BE 0x2D28E457 2 0xF92FFDE9
0x60143E4B 0x37E4C558 0 0x20040448
0x60143E4B 0x37E4C558 1 0x77F4FF5B
0x60143E4B 0x37E4C558 2 0x57F0FB13
0xBE024F92 0x4DA2DD64 0 0x0C024D00
0xBE024F92 0x4DA2DD64 1 0xFFA2DFF6
0xBE024F92 0x4DA2DD64 2 0xF3A092F6
0x364F475A 0x7E8E5F7B 0 0x360E475A
0x364F475A 0x7E8E5F7B 1 0x7ECF5F7B
0x364F475A 0x7E8E5F7B 2 0x48C11821
0x0342D6C5 0xF8395671 0 0x00005641
0x0342D6C5 0xF8395671 1 0xFB7BD6F5
0x0342D6C5 0xF8395671 2 0xFB7B80B4
0xE46AFB81 0x1A6AB1C5 0 0x006AB181
0xE46AFB81 0x1A6AB1C5 1 0xFE6AFBC5
0xE46AFB81 0x1A6AB1C5 2 0xFE004A44
0x200E3EA2 0x9C4907CA 0 0x00080682
0x200E3EA2 0x9C4907CA 1 0xBC4F3FEA
0x200E3EA2 0x9C4907CA 2 0xBC473968
0x58B7CC89 0x1E6CC2D8 0 0x1824C088
0x58B7CC89 0x1E6CC2D8 1 0x5EFFCED9
0x58B7CC89 0x1E6CC2D8 2 0x46DB0E51
0xCB94FB25 0x609F0859 0 0x40940801
0xCB94FB25 0x609F0859 1 0xEB9FFB7D
0xCB94FB25 0x609F0859 2 0xAB0BF37C
0x85E89FB5 0x9D223D73 0 0x85201D31
0x85E89FB5 0x9D223D73 1 0x9DEABFF7
0x85E89FB5 0x9D223D73 2 0x18CAA2C6
0x173613CD 0x0221F40D 0 0x0220100D
0x173613CD 0x0221F40D 1 0x1737F7CD
0x173613CD 0x0221F40D 2 0x1517E7C0
*/
