// Digital circuit control-unit.dig as structural Verilog
module control_unit (
  input  [6:0] opcode,
  input  [6:0] funct7,
  input  [2:0] funct3,
  output ALUSrc,
  output [1:0] IMMSrc,
  output [3:0] ALUOp,
  output RegWrite
);

  wire and_1_out, and_2_out, and_3_out, and_4_out, and_5_out, and_6_out, and_7_out, and_8_out, and_9_out,
       and_10_out, and_11_out, any, decoder_1_out_0, decoder_1_out_1, decoder_1_out_2, decoder_1_out_5,
       decoder_1_out_6, decoder_1_out_7, F7sub, F7zero, IsI, IsR;
  wire [3:0] priorityencoder_1_num;
  wire [7:7] rom_1_d;

  Comparator #(.Bits(7)) comparator_1 (.a(opcode), .b(7'b0110011), .eq(IsR));  // open: gt, lt
  Comparator #(.Bits(7)) comparator_2 (.a(opcode), .b(7'b0010011), .eq(IsI));  // open: gt, lt
  Comparator #(.Bits(7)) comparator_3 (.a(funct7), .b({7{1'b0}}), .eq(F7zero));  // open: gt, lt
  Comparator #(.Bits(7)) comparator_4 (.a(funct7), .b(7'b0100000), .eq(F7sub));  // open: gt, lt
  Decoder #(.Selector_Bits(3)) decoder_1 (
    .sel(funct3), .out_0(decoder_1_out_0), .out_1(decoder_1_out_1), .out_2(decoder_1_out_2),
    .out_5(decoder_1_out_5), .out_6(decoder_1_out_6), .out_7(decoder_1_out_7));  // open: out_3, out_4
  and and_1 (and_1_out, IsR, decoder_1_out_0, F7zero);
  and and_2 (and_2_out, IsR, decoder_1_out_0, F7sub);
  and and_3 (and_3_out, IsR, decoder_1_out_7, F7zero);
  and and_4 (and_4_out, IsR, decoder_1_out_6, F7zero);
  and and_5 (and_5_out, IsR, decoder_1_out_2, F7zero);
  and and_6 (and_6_out, IsR, decoder_1_out_1, F7zero);
  and and_7 (and_7_out, IsR, decoder_1_out_5, F7zero);
  and and_8 (and_8_out, IsR, decoder_1_out_5, F7sub);
  and and_9 (and_9_out, IsI, decoder_1_out_0);
  and and_10 (and_10_out, IsI, decoder_1_out_2);
  and and_11 (and_11_out, IsI, decoder_1_out_7);
  PriorityEncoder #(.Selector_Bits(4)) priorityencoder_1 (
    .in0(and_1_out), .in1(and_2_out), .in2(and_3_out), .in3(and_4_out), .in4(and_5_out), .in5(and_9_out),
    .in6(and_10_out), .in7(and_11_out), .in8(and_6_out), .in9(and_7_out), .in10(and_8_out), .in11(1'b0),
    .in12(1'b0), .in13(1'b0), .in14(1'b0), .in15(1'b0), .num(priorityencoder_1_num), .any(any));
  ROM #(.AddrBits(4), .Bits(8)) rom_1 (.A(priorityencoder_1_num), .sel(1'b1), .D({rom_1_d[7], ALUSrc, IMMSrc, ALUOp}));
  and and_12 (RegWrite, any, rom_1_d[7]);

  // Notes on the sheet:
  //   contents of rom_1 (hex, n*v repeats v):
  //   82,86,80,81,87,c2,c7,c0,84,85,88,5*0,c2,0,c7,4*0,c0,c2,0,c7,4*0
  //   ,c0,82,84,87,0,0,85,81,80,86,4*0,88
endmodule
