// Digital circuit cpu.dig as structural Verilog
module cpu (
  input  clk,
  output [31:0] ReadData1,
  output [31:0] ReadData2
);

  wire control_unit_1_alusrc, control_unit_1_regwrite;
  wire [3:0] control_unit_1_aluop;
  wire [31:0] add_1_s, bitextender_1_out, Instruction_Memory_d, multiplexer_1_out, PC_q, WriteD;

  Register #(.Bits(32), .isProgramCounter("true"), .Default(0)) PC (.D(add_1_s), .C(clk), .en(1'b1), .Q(PC_q));
  Add #(.Bits(32)) add_1 (.a(32'h4), .b(PC_q), .c_i(1'b0), .s(add_1_s));  // open: c_o
  ROM #(.AddrBits(10), .isProgramMemory("true"), .Bits(32)) Instruction_Memory (
    .A(PC_q[11:2]), .sel(1'b1), .D(Instruction_Memory_d));
  BitExtender #(.inputBits(12), .outputBits(32)) bitextender_1 (
    .in(Instruction_Memory_d[31:20]), .out(bitextender_1_out));
  control_unit control_unit_1 (
    .opcode(Instruction_Memory_d[6:0]), .funct7(Instruction_Memory_d[31:25]),
    .funct3(Instruction_Memory_d[14:12]), .ALUSrc(control_unit_1_alusrc), .ALUOp(control_unit_1_aluop),
    .RegWrite(control_unit_1_regwrite));  // open: IMMSrc
  register_file register_file_1 (
    .ReadReg1(Instruction_Memory_d[19:15]), .ReadReg2(Instruction_Memory_d[24:20]),
    .WriteReg(Instruction_Memory_d[11:7]), .WriteData(WriteD), .RegWrite(control_unit_1_regwrite), .clk(clk),
    .ReadData1(ReadData1), .ReadData2(ReadData2));
  Multiplexer #(.Bits(32)) multiplexer_1 (
    .sel(control_unit_1_alusrc), .in_0(ReadData2), .in_1(bitextender_1_out), .out(multiplexer_1_out));
  alu alu_1 (.A(ReadData1), .B(multiplexer_1_out), .ALUOp(control_unit_1_aluop), .Result(WriteD));  // open: FlagZ

  // Other names for the same wires on the sheet: clock = clk

  // Notes on the sheet:
  //   contents of Instruction_Memory (hex, n*v repeats v):
  //   fec00213,7f020293,70128313,53130393,12337713,71c77793,5417f893
  //   ,13722913,292993,9aa13,ffda2a93,5aab13,b0013,fec22b93,b8013,fa65ac13
  //   ,c0013,22c93,c8013,2585ad13,d0013,fff22d93,d8013,628233,520333
  //   ,28333,30033,40628233,40520333,40030333,40030033,72e233,26033
  //   ,62e233,26033,72f433,47033,437433,47033,1f00693,100813,d81e33
  //   ,400193,329133,2000093,1294b3,2e0033,48033,de5eb3,335fb3,1fe8033
  //   ,40de5f33,40335fb3,4032d533,1ff0033,10f5633,c50033,ce24b3,1c62533
  //   ,5320b3,62a133,52a1b3,a48033,208033,18033
endmodule

/* Test case cpu:
clk ReadData1 ReadData2
0 0 0                  # addi x4, x0, -20
C (-20) 0              # addi x5, x4, 0x7F0
C 2012 0               # addi x6, x5, 0x701
C 3805 0               # addi x7, x6, 0x531
C 3805 0               # andi x14, x6, 0x123
C 1 0                  # andi x15, x14, 0x71C
C 0 0                  # andi x17, x15, 0x541
C (-20) 0              # slti x18, x4, 311
C 1 0                  # slti x19, x18, 2
C 1 0                  # slti x20, x19, 0
C 0 0                  # slti x21, x20, -3
C 0 2012               # slti x22, x21, 5
C 1 0                  # addi x0,  x22, 0
C (-20) 0              # slti x23, x4,  -20
C 0 0                  # addi x0,  x23, 0
C 0 3805               # slti x24, x11, -90
C 0 0                  # addi x0,  x24, 0
C (-20) 0              # slti x25, x4,  0
C 1 0                  # addi x0,  x25, 0
C 0 0                  # slti x26, x11, 600
C 1 0                  # addi x0,  x26, 0
C (-20) 0              # slti x27, x4,  -1
C 1 0                  # addi x0,  x27, 0
C 2012 3805            # add x4, x5, x6
C 5817 2012            # add x6, x4, x5
C 2012 0               # add x6, x5, x0
C 2012 0               # add x0, x6, x0
C 2012 2012            # sub x4, x5, x6
C 0 2012               # sub x6, x4, x5
C (-2012) 0            # sub x6, x6, x0
C (-2012) 0            # sub x0, x6, x0
C 2012 5134            # or x4, x5, x7
C 6110 0               # or x0, x4, x0
C 2012 (-2012)         # or x4, x5, x6
C (-4) 0               # or x0, x4, x0
C 2012 5134            # and x8, x5, x7
C 1036 0               # and x0, x8, x0
C (-2012) (-4)         # and x8, x6, x4
C (-2012) 0            # and x0, x8, x0
C 0 0                  # addi x13, x0, 31
C 0 0                  # addi x16, x0, 1
C 1 31                 # sll x28, x16, x13
C 0 (-4)               # addi x3, x0, 4
C 2012 4               # sll x2, x5, x3
C 0 0                  # addi x1, x0, 32
C 2012 32              # sll x9, x5, x1
C (-2147483648) 32192  # add x0, x28, x2
C 2012 0               # add x0, x9, x0
C (-2147483648) 31     # srl x29, x28, x13
C (-2012) 4            # srl x31, x6, x3
C 1 268435330          # add x0, x29, x31
C (-2147483648) 31     # sra x30, x28, x13
C (-2012) 4            # sra x31, x6, x3
C 2012 4               # sra x10, x5, x3
C (-1) (-126)          # add x0, x30, x31
C (-1) 1               # srl x12, x30, x16
C 125 2147483647       # add x0, x10, x12
C (-2147483648) 2147483647 # slt x9, x28, x12
C 2147483647 (-2147483648) # slt x10, x12, x28
C (-2012) 2012         # slt x1, x6, x5
C 2012 (-2012)         # slt x2, x5, x6
C 2012 2012            # slt x3, x5, x5
C 1 0                  # add x0, x9, x10
C 1 0                  # add x0, x1, x2
C 0 0                  # add x0, x3, x0
*/
