// Digital circuit register-file.dig as structural Verilog
module register_file (
  input  [4:0] ReadReg1,
  input  [4:0] ReadReg2,
  input  [4:0] WriteReg,
  input  [31:0] WriteData,
  input  RegWrite,
  input  clk,
  output [31:0] ReadData1,
  output [31:0] ReadData2
);

  wire dec1, dec2, dec3, dec4, dec5, dec6, dec7, dec8, dec9, dec10, dec11, dec12, dec13, dec14, dec15, dec16,
       dec17, dec18, dec19, dec20, dec21, dec22, dec23, dec24, dec25, dec26, dec27, dec28, dec29, dec30,
       dec31, en1, en2, en3, en4, en5, en6, en7, en8, en9, en10, en11, en12, en13, en14, en15, en16, en17,
       en18, en19, en20, en21, en22, en23, en24, en25, en26, en27, en28, en29, en30, en31;
  wire [31:0] r1, r2, r3, r4, r5, r6, r7, r8, r9, r10, r11, r12, r13, r14, r15, r16, r17, r18, r19, r20, r21,
       r22, r23, r24, r25, r26, r27, r28, r29, r30, r31;

  Decoder #(.Selector_Bits(5)) decoder_1 (
    .sel(WriteReg), .out_1(dec1), .out_2(dec2), .out_3(dec3), .out_4(dec4), .out_5(dec5), .out_6(dec6),
    .out_7(dec7), .out_8(dec8), .out_9(dec9), .out_10(dec10), .out_11(dec11), .out_12(dec12), .out_13(dec13),
    .out_14(dec14), .out_15(dec15), .out_16(dec16), .out_17(dec17), .out_18(dec18), .out_19(dec19),
    .out_20(dec20), .out_21(dec21), .out_22(dec22), .out_23(dec23), .out_24(dec24), .out_25(dec25),
    .out_26(dec26), .out_27(dec27), .out_28(dec28), .out_29(dec29), .out_30(dec30), .out_31(dec31));  // open: out_0
  and and_1 (en1, dec1, RegWrite);
  and and_2 (en2, dec2, RegWrite);
  and and_3 (en3, dec3, RegWrite);
  and and_4 (en4, dec4, RegWrite);
  and and_5 (en5, dec5, RegWrite);
  and and_6 (en6, dec6, RegWrite);
  and and_7 (en7, dec7, RegWrite);
  and and_8 (en8, dec8, RegWrite);
  and and_9 (en9, dec9, RegWrite);
  and and_10 (en10, dec10, RegWrite);
  and and_11 (en11, dec11, RegWrite);
  and and_12 (en12, dec12, RegWrite);
  and and_13 (en13, dec13, RegWrite);
  and and_14 (en14, dec14, RegWrite);
  and and_15 (en15, dec15, RegWrite);
  and and_16 (en16, dec16, RegWrite);
  and and_17 (en17, dec17, RegWrite);
  and and_18 (en18, dec18, RegWrite);
  and and_19 (en19, dec19, RegWrite);
  and and_20 (en20, dec20, RegWrite);
  and and_21 (en21, dec21, RegWrite);
  and and_22 (en22, dec22, RegWrite);
  and and_23 (en23, dec23, RegWrite);
  and and_24 (en24, dec24, RegWrite);
  and and_25 (en25, dec25, RegWrite);
  and and_26 (en26, dec26, RegWrite);
  and and_27 (en27, dec27, RegWrite);
  and and_28 (en28, dec28, RegWrite);
  and and_29 (en29, dec29, RegWrite);
  and and_30 (en30, dec30, RegWrite);
  and and_31 (en31, dec31, RegWrite);
  Register #(.Bits(32)) x1 (.D(WriteData), .C(clk), .en(en1), .Q(r1));
  Register #(.Bits(32)) x2 (.D(WriteData), .C(clk), .en(en2), .Q(r2));
  Register #(.Bits(32)) x3 (.D(WriteData), .C(clk), .en(en3), .Q(r3));
  Register #(.Bits(32)) x4 (.D(WriteData), .C(clk), .en(en4), .Q(r4));
  Register #(.Bits(32)) x5 (.D(WriteData), .C(clk), .en(en5), .Q(r5));
  Register #(.Bits(32)) x6 (.D(WriteData), .C(clk), .en(en6), .Q(r6));
  Register #(.Bits(32)) x7 (.D(WriteData), .C(clk), .en(en7), .Q(r7));
  Register #(.Bits(32)) x8 (.D(WriteData), .C(clk), .en(en8), .Q(r8));
  Register #(.Bits(32)) x9 (.D(WriteData), .C(clk), .en(en9), .Q(r9));
  Register #(.Bits(32)) x10 (.D(WriteData), .C(clk), .en(en10), .Q(r10));
  Register #(.Bits(32)) x11 (.D(WriteData), .C(clk), .en(en11), .Q(r11));
  Register #(.Bits(32)) x12 (.D(WriteData), .C(clk), .en(en12), .Q(r12));
  Register #(.Bits(32)) x13 (.D(WriteData), .C(clk), .en(en13), .Q(r13));
  Register #(.Bits(32)) x14 (.D(WriteData), .C(clk), .en(en14), .Q(r14));
  Register #(.Bits(32)) x15 (.D(WriteData), .C(clk), .en(en15), .Q(r15));
  Register #(.Bits(32)) x16 (.D(WriteData), .C(clk), .en(en16), .Q(r16));
  Register #(.Bits(32)) x17 (.D(WriteData), .C(clk), .en(en17), .Q(r17));
  Register #(.Bits(32)) x18 (.D(WriteData), .C(clk), .en(en18), .Q(r18));
  Register #(.Bits(32)) x19 (.D(WriteData), .C(clk), .en(en19), .Q(r19));
  Register #(.Bits(32)) x20 (.D(WriteData), .C(clk), .en(en20), .Q(r20));
  Register #(.Bits(32)) x21 (.D(WriteData), .C(clk), .en(en21), .Q(r21));
  Register #(.Bits(32)) x22 (.D(WriteData), .C(clk), .en(en22), .Q(r22));
  Register #(.Bits(32)) x23 (.D(WriteData), .C(clk), .en(en23), .Q(r23));
  Register #(.Bits(32)) x24 (.D(WriteData), .C(clk), .en(en24), .Q(r24));
  Register #(.Bits(32)) x25 (.D(WriteData), .C(clk), .en(en25), .Q(r25));
  Register #(.Bits(32)) x26 (.D(WriteData), .C(clk), .en(en26), .Q(r26));
  Register #(.Bits(32)) x27 (.D(WriteData), .C(clk), .en(en27), .Q(r27));
  Register #(.Bits(32)) x28 (.D(WriteData), .C(clk), .en(en28), .Q(r28));
  Register #(.Bits(32)) x29 (.D(WriteData), .C(clk), .en(en29), .Q(r29));
  Register #(.Bits(32)) x30 (.D(WriteData), .C(clk), .en(en30), .Q(r30));
  Register #(.Bits(32)) x31 (.D(WriteData), .C(clk), .en(en31), .Q(r31));
  Multiplexer #(.Selector_Bits(5), .Bits(32)) multiplexer_1 (
    .sel(ReadReg1), .in_0({32{1'b0}}), .in_1(r1), .in_2(r2), .in_3(r3), .in_4(r4), .in_5(r5), .in_6(r6),
    .in_7(r7), .in_8(r8), .in_9(r9), .in_10(r10), .in_11(r11), .in_12(r12), .in_13(r13), .in_14(r14),
    .in_15(r15), .in_16(r16), .in_17(r17), .in_18(r18), .in_19(r19), .in_20(r20), .in_21(r21), .in_22(r22),
    .in_23(r23), .in_24(r24), .in_25(r25), .in_26(r26), .in_27(r27), .in_28(r28), .in_29(r29), .in_30(r30),
    .in_31(r31), .out(ReadData1));
  Multiplexer #(.Selector_Bits(5), .Bits(32)) multiplexer_2 (
    .sel(ReadReg2), .in_0({32{1'b0}}), .in_1(r1), .in_2(r2), .in_3(r3), .in_4(r4), .in_5(r5), .in_6(r6),
    .in_7(r7), .in_8(r8), .in_9(r9), .in_10(r10), .in_11(r11), .in_12(r12), .in_13(r13), .in_14(r14),
    .in_15(r15), .in_16(r16), .in_17(r17), .in_18(r18), .in_19(r19), .in_20(r20), .in_21(r21), .in_22(r22),
    .in_23(r23), .in_24(r24), .in_25(r25), .in_26(r26), .in_27(r27), .in_28(r28), .in_29(r29), .in_30(r30),
    .in_31(r31), .out(ReadData2));

  // Other names for the same wires on the sheet: RR1[4:0] = ReadReg1; RR2[4:0] = ReadReg2; RW = RegWrite;
  //   WD[31:0] = WriteData; WR[4:0] = WriteReg
endmodule

/* Test case regfile:
clk RegWrite WriteReg WriteData ReadReg1 ReadReg2 ReadData1 ReadData2
# write x1 = 5
C 1 1 5 1 0 5 0
# writes to x0 are ignored
C 1 0 99 0 1 0 5
# RegWrite = 0 must not write x2
C 0 2 7 2 1 0 5
# write x31 = -1
C 1 31 0xFFFFFFFF 31 1 0xFFFFFFFF 5
# reads change immediately, no clock needed
0 0 0 0 1 31 5 0xFFFFFFFF
# no rising edge -> no write, even with RegWrite = 1
0 1 3 42 3 0 0 0
# write x3 = 42, read same register on both ports
C 1 3 42 3 3 42 42
# overwrite x1; x3 unchanged
C 1 1 0x80000000 1 3 0x80000000 42
*/
