// Digital circuit slt-unit.dig as structural Verilog
module slt_unit (
  input  Sign,
  input  Overflow,
  output Out
);

  xor xor_1 (Out, Sign, Overflow);
endmodule

/* Test case slt-unit tests:
Sign Overflow Out
0 0 0
0 1 1
1 0 1
1 1 0
*/
